# Fritzing sketch mega_ky-033 (saved by Fritzing 0.9.9b)

parts:
  Bauteil1 = KY-033 Tracing Black White Line Hunting Sensor Module For Arduino
  Bauteil2 = Arduino Mega 2560 (Rev3)

nets:
  GND: Bauteil1.GND, Bauteil2.GND
  N1: Bauteil1.V+, Bauteil2.5V
  N2: Bauteil1.S, Bauteil2.D40

custom parts:
  KY-033 Tracing Black White Line Hunting Sensor Module For Arduino: Tracing Black White Line Hunting Sensor Module For Arduino Description: This is KY-033 tracking sensor. The KY-033 measures the intensity of infrared radiation and delivers it as an analog output voltage. Features: Operating voltage: 2.5 - 12V(cannot over12V) working current: 18mA-20mA at 5V Enhanced accuracy Documents: http://www.vishay.com/docs/83760/tcrt5000.pdf
