# Fritzing sketch mega_3xky-033 (saved by Fritzing 0.9.9b)
breadboards: 1

parts:
  Bauteil1 = Arduino Mega 2560 (Rev3)
  Bauteil2 = KY-033 Tracing Black White Line Hunting Sensor Module For Arduino
  Bauteil3 = KY-033 Tracing Black White Line Hunting Sensor Module For Arduino
  Bauteil4 = KY-033 Tracing Black White Line Hunting Sensor Module For Arduino

nets:
  N1: Bauteil1.5V, Bauteil2.V+, Bauteil3.V+, Bauteil4.V+
  GND: Bauteil1.GND, Bauteil2.GND, Bauteil3.GND, Bauteil4.GND
  N2: Bauteil1.D30, Bauteil2.S
  N3: Bauteil1.D32, Bauteil3.S
  N4: Bauteil1.D34, Bauteil4.S

custom parts:
  KY-033 Tracing Black White Line Hunting Sensor Module For Arduino: Tracing Black White Line Hunting Sensor Module For Arduino Description: This is KY-033 tracking sensor. The KY-033 measures the intensity of infrared radiation and delivers it as an analog output voltage. Features: Operating voltage: 2.5 - 12V(cannot over12V) working current: 18mA-20mA at 5V Enhanced accuracy Documents: http://www.vishay.com/docs/83760/tcrt5000.pdf
