# Fritzing sketch mega_l298n_4xdc-motor (saved by Fritzing 0.9.9b)

parts:
  Bauteil1 = Arduino Mega 2560 (Rev3)
  L298N1 = L298N DC motor driver
  M1 = gear-motor
  M2 = gear-motor
  M3 = gear-motor
  M4 = gear-motor

nets:
  VIN: Bauteil1.VIN, L298N1.5V
  N1: Bauteil1.D2_PWM, L298N1.ENB
  N2: Bauteil1.D3_PWM, L298N1.IN4
  N3: Bauteil1.D4_PWM, L298N1.IN3
  N4: Bauteil1.D5_PWM, L298N1.IN2
  N5: Bauteil1.D6_PWM, L298N1.IN1
  N6: Bauteil1.D7_PWM, L298N1.ENA
  N7: L298N1.OUT1, M1.pin_2, M2.pin_2
  N8: L298N1.OUT2, M1.pin_1, M2.pin_1
  N9: L298N1.OUT3, M3.pin_1, M4.pin_1
  N10: L298N1.OUT4, M3.pin_2, M4.pin_2

notes:
  12 V Power Source

custom parts:
  L298N DC motor driver: 2x DC motor driver with 78M05 positive voltage regulator (7..35 V) L298N: max 46 V, 2 A Set 5 V Enable jumper to enable 5 V regultor (needed for the L298N) and +5 V output at screw terminal or supply external +5 V at screw terminal Set ENA and/or ENB to +5 V to enable motor permanently or supply ENA and/or ENB with PWM signal IN1 and IN2 set rotation directory for motor A (OUT1/OUT2) IN2 and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
