# Fritzing sketch Nano_HC-SR04 (saved by Fritzing 0.9.9b)

parts:
  Nano1 = Arduino Nano v2.3
  HC-SR04_Sensor_1 = HC-SR04 Ultrasonic Distance Sensor

nets:
  N1: Nano1.D10, HC-SR04_Sensor_1.ECHO
  N2: Nano1.D11, HC-SR04_Sensor_1.TRIG
  3V3: Nano1.3V3, HC-SR04_Sensor_1.VCC
  VIN: Nano1.VIN, HC-SR04_Sensor_1.GND
