# Fritzing sketch Connect_ESP8266 (saved by Fritzing 0.9.9b)

parts:
  Bauteil1 = Arduino Nano (Rev3.0)
  M1 = ESP-01 Breakout Board Breadboard Adapter [part_number=ESP8266]

nets:
  N1: Bauteil1.GND, M1.GP0
  N2: Bauteil1.D2, M1.TXD
  N3: Bauteil1.D3, M1.RXD
  3V3: Bauteil1.3V3, M1.VCC

custom parts:
  ESP-01 Breakout Board Breadboard Adapter: Generic WiFi Module based on the ESP8266 with onboard PCB antenna and UART communications with breadboard friendly breakout board attached.
